# Fritzing sketch schematic (saved by Fritzing 0.9.6b)

parts:
  R1 = Resistor [tolerance=±5% power=0.25 resistance=4.7 package=THT]
  DS1 = DS18B20 1-Wire Temperature Sensor [part_number=DS18B20]
  DS2 = DS18B20 1-Wire Temperature Sensor [part_number=DS18B20]
  DS3 = DS18B20 1-Wire Temperature Sensor [part_number=DS18B20]
  DS4 = DS18B20 1-Wire Temperature Sensor [part_number=DS18B20]
  Part1 = Arduino Nano (Rev3.0) (ICSP)
  R2 = Resistor [tolerance=±5% power=0.25 resistance=4.7 package=THT]  # not connected
  R3 = Resistor [tolerance=±5% power=0.25 resistance=4.7 package=THT]
  R4 = Resistor [tolerance=±5% power=0.25 resistance=4.7 package=THT]
  R5 = Resistor [tolerance=±5% power=0.25 resistance=4.7 package=THT]
  Mod1 = KY-019
  LED1 = LEDs [package=led10mm]
  Part2 = LCD1602-I2C_
  U1 = SWITCH-SPST-2 [package=r_sw_th]  # not connected
  U2 = SWITCH-SPST-2 [package=r_sw_th]  # not connected

nets:
  VDD: R1.Pin_0, DS1.VDD, DS2.VDD, DS3.VDD, DS4.VDD, Part1.5V, R3.Pin_0, R4.Pin_0, R5.Pin_0, Mod1.connector1, Part2.connector1
  N1: R1.Pin_1, DS1.DQ, Part1.D2
  GND: DS1.GND, DS2.GND, DS3.GND, DS4.GND, Part1.GND, Mod1.connector0, Part2.connector0
  N2: DS2.DQ, Part1.D4, R4.Pin_1
  N3: DS3.DQ, Part1.D6, R3.Pin_1
  N4: DS4.DQ, Part1.D8, R5.Pin_1
  N5: Part1.D10, Mod1.connector2
  N6: Part1.A5, Part2.connector3
  N7: Part1.A4, Part2.connector2
  N8: Mod1.connector5, LED1.C
